# Fritzing sketch FINAL-PROJECT (saved by Fritzing 0.8.7b)
breadboards: 1

parts:
  Part1 = Arduino Mega ADK (Rev3)
  R1 = Resistor [tolerance=±5% resistance=220 package=THT]
  R2 = Resistor [tolerance=±5% resistance=220 package=THT]
  C1 = Electrolytic Capacitor [capacitance=1µF package="100 mil [THT, electrolytic]"]

nets:
  N1: Part1.A0, R1.Pin_1, R2.Pin_0, C1.+
  N2: Part1.D13_PWM, R1.Pin_0
  N3: Part1.D10_PWM, R2.Pin_1
  N4: Part1.GND, C1.-

notes:
  CAPACITANCE READING USING ARDUINO
  POLESTICO-SUAREZ
