# Fritzing sketch MIDTERM-PROJECT (saved by Fritzing 0.8.7b)
breadboards: 1

parts:
  Part1 = Arduino Mega 2560 (Rev3)
  R4 = Resistor [tolerance=±5% resistance=1k package=THT]
  R5 = Resistor [tolerance=±5% resistance=1k package=THT]
  R6 = Resistor [tolerance=±5% resistance=1k package=THT]
  R7 = Resistor [tolerance=±5% resistance=150 package=THT]
  R8 = Resistor [tolerance=±5% resistance=470 package=THT]
  R9 = Resistor [tolerance=±5% resistance=220 package=THT]

nets:
  N1: Part1.A0, R6.Pin_1, R7.Pin_1
  N2: Part1.A1, R5.Pin_1, R8.Pin_0
  N3: Part1.A2, R4.Pin_1, R9.Pin_1
  N4: Part1.5V, R7.Pin_0, R8.Pin_1, R9.Pin_0
  N5: Part1.GND, R4.Pin_0, R5.Pin_0, R6.Pin_0

notes:
  DELTA TO WYE TRANSFORMATION
  15. POLESTICO-SUAREZ

// code stored in the sketch: DELTA-Y_TRANSFORMATION.ino
const int sensorPin1 = A2; 
const int sensorPin2 = A3;
const int sensorPin3 = A4;
int sensorValue1 = 0;   
int sensorValue2 = 0;
int sensorValue3 = 0;
float Vin = 5;
float Vout1 = 0;  
float Vout2 = 0;
float Vout3 = 0;
float Rref1 = 1000; 
float Rref2 = 1000;
float Rref3 = 1000;
float r1 = 0; 
float r2 = 0;  
float r3 = 0;
float rA=0,rB=0,rC=0;
void setup ()
{
  Serial.begin(9600);      // Initialize serial communications at 9600 bps
}
void getR1(){
  sensorValue1 = analogRead(sensorPin1);
  Vout1 = (Vin * sensorValue1) / 1023;    
  r1 = Rref1 * (1 / ((Vin / Vout1) - 1));  
  Serial.print("Resistor 1: ");                  
  Serial.println(r1);                
  delay(1000);
  }
  void getR2(){
  sensorValue2 = analogRead(sensorPin2);
  Vout2 = (Vin * sensorValue2) / 1024;    
  r2 = Rref2 * (1 / ((Vin / Vout2) - 1));  
  Serial.print("Resistor 2: ");                  
  Serial.println(r2);                     // Give calculated resistance in Serial Monitor
  delay(1000);
  }
  void getR3(){
  sensorValue3 = analogRead(sensorPin3);
  Vout3 = (Vin * sensorValue3) / 1024;    
  r3 = Rref3 * (1 / ((Vin / Vout3) - 1));  
  Serial.print("Resistor 3: ");                  
  Serial.println(r3);                     // Give calculated resistance in Serial Monitor
    delay(1000);
  }
void loop ()
{
  Serial.println("******************************************");
  Serial.println("*******Delta to Y Transformation**********");
  Serial.println("-DELTA RESISTOR'S VALUE-");
  getR1();
  getR2();
  getR3();
  Serial.println("-Y RESISTOR'S VALUE-");
  delay(2000);
   rA=(r2*r3)/(r1+r2+r3);
   rB=(r3*r1)/(r1+r2+r3);
    rC=(r1*r2)/(r1+r2+r3);
    Serial.print("Resistor A:");
    Serial.println(rA);
    Serial.print("Resistor B:");
    Serial.println(rB);
    Serial.print("Resistor C:");
    Serial.println(rC);
    Serial.println("********************************************");
delay(2000);
}

// code stored in the sketch: Y2D.ino
const int sensorPin1 = A0; 
const int sensorPin2 = A1;
const int sensorPin3 = A2;
int sensorValue1 = 0;   
int sensorValue2 = 0;
int sensorValue3 = 0;
float Vin = 5;
float Vout1 = 0;  
float Vout2 = 0;
float Vout3 = 0;
float Rref1 = 1000; 
float Rref2 = 1000;
float Rref3 = 1000;
float r1 = 0; 
float r2 = 0;  
float r3 = 0;
float ra=0,rb=0,rc=0;
void setup ()
{
  Serial.begin(9600);      // Initialize serial communications at 9600 bps
}
void getR1(){
  sensorValue1 = analogRead(sensorPin1);
  Vout1 = (Vin * sensorValue1) / 1024;    
  ra = Rref1 * (1 / ((Vin / Vout1) - 1));  
  Serial.print("Resistor 1: ");                  
  Serial.println(ra);                
  delay(1000);
  }
  void getR2(){
  sensorValue2 = analogRead(sensorPin2);
  Vout2 = (Vin * sensorValue2) / 1023;    
  rb = Rref2 * (1 / ((Vin / Vout2) - 1));  
  Serial.print("Resistor 2: ");                  
  Serial.println(rb);                     // Give calculated resistance in Serial Monitor
  delay(1000);
  }
  void getR3(){
  sensorValue3 = analogRead(sensorPin3);
  Vout3 = (Vin * sensorValue3) / 1023;    
  rc = Rref3 * (1 / ((Vin / Vout3) - 1));  
  Serial.print("Resistor 3: ");                  
  Serial.println(rc);                     // Give calculated resistance in Serial Monitor
    delay(1000);
  }
void loop ()
{
  Serial.println("------------------------------------------");
  Serial.println("Y to Delta");
  Serial.println("Reading Resistors. . . . ");
  getR1();
  getR2();
  getR3();
  Serial.println("Computing.....");
  delay(2000);
    r1=((ra*rb)+(rb*rc)+(rc*ra))/ra;
    r2=((ra*rb)+(rb*rc)+(rc*ra))/rb;
    r3=((ra*rb)+(rb*rc)+(rc*ra))/rc;
    Serial.print("Resistor A:");
    Serial.println(r1);
    Serial.print("Resistor B:");
    Serial.println(r2);
    Serial.print("Resistor C:");
    Serial.println(r3);
    Serial.println("------------------------------------------");
delay(2000);
}
